// Logisim project instruction_memory.circ as structural Verilog: 1 circuit, main circuit instruction_rom
module instruction_rom (
  input  [7:0] add_i,
  output [31:0] data_o
);

  ROM #(.addrWidth(6), .dataWidth(32)) rom_1 (.addr(add_i[7:2]), .data(data_o));
endmodule
