// Logisim project registers_bank_incomplete.circ as structural Verilog: 3 circuits, main circuit alu
module registers_bank (
  input  clk_i,
  input  rst_i,
  input  [31:0] rd_data_i,
  input  [4:0] rs1_add_i,
  input  [4:0] rs2_add_i,
  input  [4:0] rd_add_i,
  input  we_i,
  output [31:0] rs1_data_o,
  output [31:0] rs2_data_o
);

  wire demultiplexer_1_out0, demultiplexer_1_out1, demultiplexer_1_out2, demultiplexer_1_out3,
       demultiplexer_1_out4, demultiplexer_1_out5, demultiplexer_1_out6, demultiplexer_1_out7,
       demultiplexer_1_out8, demultiplexer_1_out9, demultiplexer_1_out10, demultiplexer_1_out11,
       demultiplexer_1_out12, demultiplexer_1_out13, demultiplexer_1_out14, demultiplexer_1_out15,
       demultiplexer_1_out16, demultiplexer_1_out17, demultiplexer_1_out18, demultiplexer_1_out19,
       demultiplexer_1_out20, demultiplexer_1_out21, demultiplexer_1_out22, demultiplexer_1_out23,
       demultiplexer_1_out24, demultiplexer_1_out25, demultiplexer_1_out26, demultiplexer_1_out27,
       demultiplexer_1_out28, demultiplexer_1_out29, demultiplexer_1_out30, demultiplexer_1_out31;
  wire [31:0] register_1_q, register_2_q, register_3_q, register_4_q, register_5_q, register_6_q,
       register_7_q, register_8_q, register_9_q, register_10_q, register_11_q, register_12_q, register_13_q,
       register_14_q, register_15_q, register_16_q, register_17_q, register_18_q, register_19_q,
       register_20_q, register_21_q, register_22_q, register_23_q, register_24_q, register_25_q,
       register_26_q, register_27_q, register_28_q, register_29_q, register_30_q, register_31_q;

  // NoConnect on demultiplexer_1_out0
  Demultiplexer #(.select(5)) demultiplexer_1 (
    .out0(demultiplexer_1_out0), .out1(demultiplexer_1_out1), .out2(demultiplexer_1_out2),
    .out3(demultiplexer_1_out3), .out4(demultiplexer_1_out4), .out5(demultiplexer_1_out5),
    .out6(demultiplexer_1_out6), .out7(demultiplexer_1_out7), .out8(demultiplexer_1_out8),
    .out9(demultiplexer_1_out9), .out10(demultiplexer_1_out10), .out11(demultiplexer_1_out11),
    .out12(demultiplexer_1_out12), .out13(demultiplexer_1_out13), .out14(demultiplexer_1_out14),
    .out15(demultiplexer_1_out15), .out16(demultiplexer_1_out16), .out17(demultiplexer_1_out17),
    .out18(demultiplexer_1_out18), .out19(demultiplexer_1_out19), .out20(demultiplexer_1_out20),
    .out21(demultiplexer_1_out21), .out22(demultiplexer_1_out22), .out23(demultiplexer_1_out23),
    .out24(demultiplexer_1_out24), .out25(demultiplexer_1_out25), .out26(demultiplexer_1_out26),
    .out27(demultiplexer_1_out27), .out28(demultiplexer_1_out28), .out29(demultiplexer_1_out29),
    .out30(demultiplexer_1_out30), .out31(demultiplexer_1_out31), .in(we_i), .sel(rd_add_i));
  Register #(.width(32)) register_1 (
    .D(rd_data_i), .en(demultiplexer_1_out1), .clk(clk_i), .Q(register_1_q), .clr(rst_i));
  Register #(.width(32)) register_2 (
    .D(rd_data_i), .en(demultiplexer_1_out2), .clk(clk_i), .Q(register_2_q), .clr(rst_i));
  Register #(.width(32)) register_3 (
    .D(rd_data_i), .en(demultiplexer_1_out3), .clk(clk_i), .Q(register_3_q), .clr(rst_i));
  Register #(.width(32)) register_4 (
    .D(rd_data_i), .en(demultiplexer_1_out4), .clk(clk_i), .Q(register_4_q), .clr(rst_i));
  Register #(.width(32)) register_5 (
    .D(rd_data_i), .en(demultiplexer_1_out5), .clk(clk_i), .Q(register_5_q), .clr(rst_i));
  Register #(.width(32)) register_6 (
    .D(rd_data_i), .en(demultiplexer_1_out6), .clk(clk_i), .Q(register_6_q), .clr(rst_i));
  Register #(.width(32)) register_7 (
    .D(rd_data_i), .en(demultiplexer_1_out7), .clk(clk_i), .Q(register_7_q), .clr(rst_i));
  Register #(.width(32)) register_8 (
    .D(rd_data_i), .en(demultiplexer_1_out8), .clk(clk_i), .Q(register_8_q), .clr(rst_i));
  Register #(.width(32)) register_9 (
    .D(rd_data_i), .en(demultiplexer_1_out9), .clk(clk_i), .Q(register_9_q), .clr(rst_i));
  Register #(.width(32)) register_10 (
    .D(rd_data_i), .en(demultiplexer_1_out10), .clk(clk_i), .Q(register_10_q), .clr(rst_i));
  Register #(.width(32)) register_11 (
    .D(rd_data_i), .en(demultiplexer_1_out11), .clk(clk_i), .Q(register_11_q));  // open: clr
  Register #(.width(32)) register_12 (
    .D(rd_data_i), .en(demultiplexer_1_out12), .clk(clk_i), .Q(register_12_q), .clr(rst_i));
  Register #(.width(32)) register_13 (
    .D(rd_data_i), .en(demultiplexer_1_out13), .clk(clk_i), .Q(register_13_q), .clr(rst_i));
  Register #(.width(32)) register_14 (
    .D(rd_data_i), .en(demultiplexer_1_out14), .clk(clk_i), .Q(register_14_q), .clr(rst_i));
  Register #(.width(32)) register_15 (
    .D(rd_data_i), .en(demultiplexer_1_out15), .clk(clk_i), .Q(register_15_q), .clr(rst_i));
  Register #(.width(32)) register_16 (
    .D(rd_data_i), .en(demultiplexer_1_out16), .clk(clk_i), .Q(register_16_q), .clr(rst_i));
  Register #(.width(32)) register_17 (
    .D(rd_data_i), .en(demultiplexer_1_out17), .clk(clk_i), .Q(register_17_q), .clr(rst_i));
  Register #(.width(32)) register_18 (
    .D(rd_data_i), .en(demultiplexer_1_out18), .clk(clk_i), .Q(register_18_q), .clr(rst_i));
  Register #(.width(32)) register_19 (
    .D(rd_data_i), .en(demultiplexer_1_out19), .clk(clk_i), .Q(register_19_q), .clr(rst_i));
  Register #(.width(32)) register_20 (
    .D(rd_data_i), .en(demultiplexer_1_out20), .clk(clk_i), .Q(register_20_q), .clr(rst_i));
  Register #(.width(32)) register_21 (
    .D(rd_data_i), .en(demultiplexer_1_out21), .clk(clk_i), .Q(register_21_q), .clr(rst_i));
  Register #(.width(32)) register_22 (
    .D(rd_data_i), .en(demultiplexer_1_out22), .clk(clk_i), .Q(register_22_q), .clr(rst_i));
  Register #(.width(32)) register_23 (
    .D(rd_data_i), .en(demultiplexer_1_out23), .clk(clk_i), .Q(register_23_q), .clr(rst_i));
  Register #(.width(32)) register_24 (
    .D(rd_data_i), .en(demultiplexer_1_out24), .clk(clk_i), .Q(register_24_q), .clr(rst_i));
  Register #(.width(32)) register_25 (
    .D(rd_data_i), .en(demultiplexer_1_out25), .clk(clk_i), .Q(register_25_q), .clr(rst_i));
  Register #(.width(32)) register_26 (
    .D(rd_data_i), .en(demultiplexer_1_out26), .clk(clk_i), .Q(register_26_q), .clr(rst_i));
  Register #(.width(32)) register_27 (
    .D(rd_data_i), .en(demultiplexer_1_out27), .clk(clk_i), .Q(register_27_q), .clr(rst_i));
  Register #(.width(32)) register_28 (
    .D(rd_data_i), .en(demultiplexer_1_out28), .clk(clk_i), .Q(register_28_q), .clr(rst_i));
  Register #(.width(32)) register_29 (
    .D(rd_data_i), .en(demultiplexer_1_out29), .clk(clk_i), .Q(register_29_q), .clr(rst_i));
  Register #(.width(32)) register_30 (
    .D(rd_data_i), .en(demultiplexer_1_out30), .clk(clk_i), .Q(register_30_q), .clr(rst_i));
  Register #(.width(32)) register_31 (
    .D(rd_data_i), .en(demultiplexer_1_out31), .clk(clk_i), .Q(register_31_q), .clr(rst_i));
  Multiplexer #(.select(5), .width(32)) multiplexer_1 (
    .in0({32{1'b0}}), .in1(register_1_q), .in2(register_2_q), .in3(register_3_q), .in4(register_4_q),
    .in5(register_5_q), .in6(register_6_q), .in7(register_7_q), .in8(register_8_q), .in9(register_9_q),
    .in10(register_10_q), .in11(register_11_q), .in12(register_12_q), .in13(register_13_q),
    .in14(register_14_q), .in15(register_15_q), .in16(register_16_q), .in17(register_17_q),
    .in18(register_18_q), .in19(register_19_q), .in20(register_20_q), .in21(register_21_q),
    .in22(register_22_q), .in23(register_23_q), .in24(register_24_q), .in25(register_25_q),
    .in26(register_26_q), .in27(register_27_q), .in28(register_28_q), .in29(register_29_q),
    .in30(register_30_q), .in31(register_31_q), .out(rs1_data_o), .sel(rs1_add_i));
  Multiplexer #(.select(5), .width(32)) multiplexer_2 (
    .in0({32{1'b0}}), .in1(register_1_q), .in2(register_2_q), .in3(register_3_q), .in4(register_4_q),
    .in5(register_5_q), .in6(register_6_q), .in7(register_7_q), .in8(register_8_q), .in9(register_9_q),
    .in10(register_10_q), .in11(register_11_q), .in12(register_12_q), .in13(register_13_q),
    .in14(register_14_q), .in15(register_15_q), .in16(register_16_q), .in17(register_17_q),
    .in18(register_18_q), .in19(register_19_q), .in20(register_20_q), .in21(register_21_q),
    .in22(register_22_q), .in23(register_23_q), .in24(register_24_q), .in25(register_25_q),
    .in26(register_26_q), .in27(register_27_q), .in28(register_28_q), .in29(register_29_q),
    .in30(register_30_q), .in31(register_31_q), .out(rs2_data_o), .sel(rs2_add_i));
endmodule

module alu (
  input  [31:0] op1_i,
  input  [31:0] op2_i,
  input  [3:0] func_i,
  output [31:0] d_o,
  output zero_o,
  output lt_o
);

  wire comparator_1_eq, comparator_1_gt, comparator_2_eq, comparator_2_gt;
  wire [0:0] comparator_1_lt, comparator_2_lt;
  wire [31:0] adder_1_out, and_1_out, or_1_out, shifter_1_out, shifter_2_out, shifter_3_out,
       subtractor_1_out, xor_1_out;

  Adder #(.width(32)) adder_1 (.a(op1_i), .b(op2_i), .out(adder_1_out), .cin(1'b0));  // open: cout
  Subtractor #(.width(32)) subtractor_1 (.a(op1_i), .b(op2_i), .out(subtractor_1_out), .bin(1'b0));  // open: bout
  Shifter #(.width(32)) shifter_1 (.in(op1_i), .\dist (op2_i[4:0]), .out(shifter_1_out));
  Shifter #(.shift("lr"), .width(32)) shifter_2 (.in(op1_i), .\dist (op2_i[4:0]), .out(shifter_2_out));
  Shifter #(.shift("ar"), .width(32)) shifter_3 (.in(op1_i), .\dist (op2_i[4:0]), .out(shifter_3_out));
  Comparator #(.width(32)) comparator_1 (
    .a(op1_i), .b(op2_i), .gt(comparator_1_gt), .eq(comparator_1_eq), .lt(comparator_1_lt[0]));
  Comparator #(.mode("unsigned"), .width(32)) comparator_2 (
    .a(op1_i), .b(op2_i), .gt(comparator_2_gt), .eq(comparator_2_eq), .lt(comparator_2_lt[0]));
  assign and_1_out = op1_i & op2_i;  // AND_Gate and_1, 32 bits wide
  assign or_1_out = op1_i | op2_i;  // OR_Gate or_1, 32 bits wide
  assign xor_1_out = op1_i ^ op2_i;  // XOR_Gate xor_1, 32 bits wide
  // NoConnect on comparator_1_gt
  // NoConnect on comparator_1_eq
  // NoConnect on comparator_2_gt
  // NoConnect on comparator_2_eq
  Multiplexer #(.select(4), .width(32)) multiplexer_1 (
    .in0({32{1'b0}}), .in1(adder_1_out), .in2(subtractor_1_out), .in3(shifter_1_out), .in4(shifter_2_out),
    .in5(shifter_3_out), .in6(and_1_out), .in7(or_1_out), .in8(xor_1_out),
    .in9({{31{1'b0}}, comparator_1_lt[0]}), .in10({{31{1'b0}}, comparator_2_lt[0]}), .in11({32{1'b0}}),
    .in12({32{1'b0}}), .in13({32{1'b0}}), .in14({32{1'b0}}), .in15({32{1'b0}}), .out(d_o), .sel(func_i));
  Comparator #(.width(32)) comparator_3 (.a(d_o), .b({32{1'b0}}), .eq(zero_o), .lt(lt_o));  // open: gt

  // Notes on the sheet:
  //   ALU
  //   Fonction de l'ALU
endmodule

module test (
  input  in_1,
  input  [4:0] in_2,
  input  [4:0] in_3,
  input  [4:0] in_4,
  input  [3:0] func_i,
  input  in_6,
  input  [31:0] instruction,
  output out_8,
  output out_9
);

  wire clock_1_out;
  wire [31:0] alu_1_d_o, registers_bank_1_rs1_data_o, registers_bank_1_rs2_data_o;

  Clock clock_1 (.out(clock_1_out));
  registers_bank registers_bank_1 (
    .clk_i(clock_1_out), .rst_i(in_1), .rd_data_i(alu_1_d_o), .rs1_add_i(in_2), .rs2_add_i(in_3),
    .rd_add_i(in_4), .we_i(in_6), .rs1_data_o(registers_bank_1_rs1_data_o),
    .rs2_data_o(registers_bank_1_rs2_data_o));
  alu alu_1 (
    .op1_i(registers_bank_1_rs1_data_o), .op2_i(registers_bank_1_rs2_data_o), .func_i(func_i),
    .d_o(alu_1_d_o), .zero_o(out_8), .lt_o(out_9));

  // Notes on the sheet:
  //   Horloge
endmodule
